# Fritzing sketch esp8266_dq_mini_temp_hum_sensor (saved by Fritzing 0.9.3b)
circuit board: 5cm x 3cm
breadboards: 1

parts:
  WeMos_D1_Mini1 = WeMos D1 Mini
  Part2 = Adafruit Si7021 Temp Humidity [part_number="Adafruit #3251"]
  Deep_Sleep_Connection = DC Motor
  VCC1 = Battery
  22k_Ohm = Resistor [tolerance=±5% resistance=220 package=THT]
  47k_Ohm1 = Resistor [tolerance=±5% resistance=220 package=THT]

nets:
  3V3: WeMos_D1_Mini1.3V3, Part2.+3V3
  N1: WeMos_D1_Mini1.5V, VCC1.+, 22k_Ohm.Pin_1
  N2: WeMos_D1_Mini1.A0, 22k_Ohm.Pin_0, 47k_Ohm1.Pin_1
  N3: WeMos_D1_Mini1.D0, Deep_Sleep_Connection.pin_2
  N4: WeMos_D1_Mini1.D1, Part2.SCL
  N5: WeMos_D1_Mini1.D2, Part2.SDA
  N6: WeMos_D1_Mini1.G, Part2.GND, VCC1.-, 47k_Ohm1.Pin_0
  N7: WeMos_D1_Mini1.RST, Deep_Sleep_Connection.pin_1

custom parts:
  Adafruit Si7021 Temp Humidity: It's summer and you're sweating and your hair's all frizzy and all you really want to know is why the weatherman said this morning that today's relative humidity would max out at a perfectly reasonable 42% when it feels more like 77%. Enter the Si7021 Temperature + Humidity Sensor - the best way to prove the weatherman wrong! This lovely sensor for Silicon labs has ± 3% relative humidity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
